// Logisim project Central Processing Unit (CPU).circ as structural Verilog: 19 circuits, main circuit 5-bit NOT Gate
module _5_bit_NOT_Gate (
  input  [4:0] in_1,
  output [4:0] out_2
);

  not not_1 (out_2[4], in_1[4]);
  not not_2 (out_2[3], in_1[3]);
  not not_3 (out_2[2], in_1[2]);
  not not_4 (out_2[1], in_1[1]);
  not not_5 (out_2[0], in_1[0]);

  // Other names for the same wires on the sheet: A0 = in_1[0]; A1 = in_1[1]; A2 = in_1[2]; A3 = in_1[3]; A4 = in_1[4];
  //   O0 = out_2[0]; O1 = out_2[1]; O2 = out_2[2]; O3 = out_2[3]; O4 = out_2[4]
endmodule

module _5_bit_Right_Rotate (
  input  [4:0] A,
  input  [2:0] Shift,
  output [4:0] O
);

  Multiplexer #(.select(3), .enable("false")) multiplexer_1 (
    .in0(A[4]), .in1(A[0]), .in2(A[1]), .in3(A[2]), .in4(A[3]), .in5(1'b0), .in6(1'b0), .in7(1'b0),
    .out(O[4]), .sel(Shift));
  Multiplexer #(.select(3), .enable("false")) multiplexer_2 (
    .in0(A[3]), .in1(A[4]), .in2(A[0]), .in3(A[1]), .in4(A[2]), .in5(1'b0), .in6(1'b0), .in7(1'b0),
    .out(O[3]), .sel(Shift));
  Multiplexer #(.select(3), .enable("false")) multiplexer_3 (
    .in0(A[2]), .in1(A[3]), .in2(A[4]), .in3(A[0]), .in4(A[1]), .in5(1'b0), .in6(1'b0), .in7(1'b0),
    .out(O[2]), .sel(Shift));
  Multiplexer #(.select(3), .enable("false")) multiplexer_4 (
    .in0(A[1]), .in1(A[2]), .in2(A[3]), .in3(A[4]), .in4(A[0]), .in5(1'b0), .in6(1'b0), .in7(1'b0),
    .out(O[1]), .sel(Shift));
  Multiplexer #(.select(3), .enable("false")) multiplexer_5 (
    .in0(A[0]), .in1(A[1]), .in2(A[2]), .in3(A[3]), .in4(A[4]), .in5(1'b0), .in6(1'b0), .in7(1'b0),
    .out(O[0]), .sel(Shift));
endmodule

module ALU (
  input  [4:0] A__4_0,
  input  OP_1_0,
  input  [4:0] B_4_0,
  output [4:0] R__4_0,
  output Sign_Flag,
  output Zero_Flag,
  output Carry_Flag
);

  wire or_1_out;
  wire [4:0] NOT, R_ROTATE;

  _5_bit_Right_Rotate u_5_bit_right_rotate_1 (.A(A__4_0), .Shift(B_4_0[2:0]), .O(R_ROTATE));
  _5_bit_NOT_Gate u_5_bit_not_1 (.in_1(A__4_0), .out_2(NOT));
  Multiplexer #(.width(5), .enable("false")) multiplexer_1 (.in0(NOT), .in1(R_ROTATE), .out(R__4_0), .sel(OP_1_0));
  or or_1 (or_1_out, R__4_0[0], R__4_0[1], R__4_0[2], R__4_0[3], R__4_0[4]);
  not not_1 (Zero_Flag, or_1_out);
  and and_1 (Carry_Flag, or_1_out, Zero_Flag);

  assign Sign_Flag = R__4_0[4];

  // Other names for the same wires on the sheet: A[4:0] = A__4_0; B[4:0] = B_4_0
endmodule

module ALU_Testing (
  input  [4:0] in_1,
  input  [4:0] in_2,
  input  in_3,
  output [4:0] out_4,
  output out_5,
  output out_6,
  output out_7
);

  ALU alu_1 (
    .A__4_0(in_1), .OP_1_0(in_3), .R__4_0(out_4), .Sign_Flag(out_6), .Zero_Flag(out_7), .B_4_0(in_2),
    .Carry_Flag(out_5));
endmodule

module _1_bit_Register (
  input  Din,
  input  Sel,
  input  Clock,
  output Dout
);

  wire multiplexer_1_out;

  Multiplexer #(.enable("false")) multiplexer_1 (.in0(Dout), .in1(Din), .out(multiplexer_1_out), .sel(Sel));
  D_Flip_Flop d_ff_1 (.clk(Clock), .D(multiplexer_1_out), .Q(Dout));  // open: Qn, preset, en, reset
endmodule

module _5_bit_Register (
  input  [4:0] Din_4_0,
  input  Sel,
  input  Clock,
  output [4:0] Dout_4_0
);

  _1_bit_Register u_1_bit_register_1 (.Din(Din_4_0[0]), .Sel(Sel), .Clock(Clock), .Dout(Dout_4_0[0]));
  _1_bit_Register u_1_bit_register_2 (.Din(Din_4_0[1]), .Sel(Sel), .Clock(Clock), .Dout(Dout_4_0[1]));
  _1_bit_Register u_1_bit_register_3 (.Din(Din_4_0[2]), .Sel(Sel), .Clock(Clock), .Dout(Dout_4_0[2]));
  _1_bit_Register u_1_bit_register_4 (.Din(Din_4_0[3]), .Sel(Sel), .Clock(Clock), .Dout(Dout_4_0[3]));
  _1_bit_Register u_1_bit_register_5 (.Din(Din_4_0[4]), .Sel(Sel), .Clock(Clock), .Dout(Dout_4_0[4]));
endmodule

module Register_Set_with_3__5_bit_Registers (
  input  [4:0] WRD,
  input  WE,
  input  [1:0] WR,
  input  Clock,
  input  [1:0] RA,
  input  [1:0] RB,
  output [4:0] A,
  output [4:0] B
);

  wire Reg0, Reg1, Reg2;
  wire [4:0] R0, R1, R2;

  Decoder #(.select(2)) decoder_1 (.out0(Reg0), .out1(Reg1), .out2(Reg2), .sel(WR), .en(WE));  // open: out3
  _5_bit_Register u_5_bit_register_1 (.Din_4_0(WRD), .Sel(Reg0), .Clock(Clock), .Dout_4_0(R0));
  _5_bit_Register u_5_bit_register_2 (.Din_4_0(WRD), .Sel(Reg1), .Clock(Clock), .Dout_4_0(R1));
  _5_bit_Register u_5_bit_register_3 (.Din_4_0(WRD), .Sel(Reg2), .Clock(Clock), .Dout_4_0(R2));
  Multiplexer #(.select(2), .width(5), .enable("false")) multiplexer_1 (
    .in0(R0), .in1(R1), .in2(R2), .out(A), .sel(RA));  // open: in3
  Multiplexer #(.select(2), .width(5), .enable("false")) multiplexer_2 (
    .in0(R0), .in1(R1), .in2(R2), .out(B), .sel(RB));  // open: in3
endmodule

module Register_Set_Testing (
  input  [1:0] RA_1_0,
  input  [1:0] RB_1_0,
  input  WE,
  input  [1:0] WR_1_0,
  input  [4:0] Wrd__4_0,
  output [4:0] A_4_0,
  output [4:0] B_4_0
);

  wire Clock_out;

  Clock Clock (.out(Clock_out));
  Register_Set_with_3__5_bit_Registers register_set_with_3_5_bit_registers_1 (
    .WRD(Wrd__4_0), .WE(WE), .WR(WR_1_0), .Clock(Clock_out), .RA(RA_1_0), .RB(RB_1_0), .A(A_4_0), .B(B_4_0));
endmodule

module _1x1_SRAM (
  input  Read_Select_1,
  input  Read_Select_2,
  input  Write_Data,
  input  Write_Select,
  input  Clock,
  output Read_Data_1,
  output Read_Data_2
);

  wire d_ff_1_q, multiplexer_1_out;

  Multiplexer #(.enable("false")) multiplexer_1 (
    .in0(d_ff_1_q), .in1(Write_Data), .out(multiplexer_1_out), .sel(Write_Select));
  D_Flip_Flop d_ff_1 (.clk(Clock), .D(multiplexer_1_out), .Q(d_ff_1_q));  // open: Qn, preset, en, reset
  and and_1 (Read_Data_1, Read_Select_1, d_ff_1_q);
  and and_2 (Read_Data_2, Read_Select_2, d_ff_1_q);
endmodule

module _1x16_SRAM (
  input  [15:0] Write_Data_15_0,
  input  Read_Select_1,
  input  Read_Select_2,
  input  Write_Select,
  input  Clock,
  output [15:0] Read_Data_1,
  output [15:0] Read_Data_2
);

  _1x1_SRAM u_1x1_sram_1 (
    .Write_Data(Write_Data_15_0[0]), .Write_Select(Read_Select_1), .Clock(Clock),
    .Read_Data_1(Read_Data_1[0]), .Read_Data_2(Read_Data_2[0]), .Read_Select_1(Read_Select_2),
    .Read_Select_2(Write_Select));
  _1x1_SRAM u_1x1_sram_2 (
    .Write_Data(Write_Data_15_0[4]), .Write_Select(Read_Select_1), .Clock(Clock),
    .Read_Data_1(Read_Data_1[4]), .Read_Data_2(Read_Data_2[4]), .Read_Select_1(Read_Select_2),
    .Read_Select_2(Write_Select));
  _1x1_SRAM u_1x1_sram_3 (
    .Write_Data(Write_Data_15_0[8]), .Write_Select(Read_Select_1), .Clock(Clock),
    .Read_Data_1(Read_Data_1[8]), .Read_Data_2(Read_Data_2[8]), .Read_Select_1(Read_Select_2),
    .Read_Select_2(Write_Select));
  _1x1_SRAM u_1x1_sram_4 (
    .Write_Data(Write_Data_15_0[12]), .Write_Select(Read_Select_1), .Clock(Clock),
    .Read_Data_1(Read_Data_1[12]), .Read_Data_2(Read_Data_2[12]), .Read_Select_1(Read_Select_2),
    .Read_Select_2(Write_Select));
  _1x1_SRAM u_1x1_sram_5 (
    .Write_Data(Write_Data_15_0[1]), .Write_Select(Read_Select_1), .Clock(Clock),
    .Read_Data_1(Read_Data_1[1]), .Read_Data_2(Read_Data_2[1]), .Read_Select_1(Read_Select_2),
    .Read_Select_2(Write_Select));
  _1x1_SRAM u_1x1_sram_6 (
    .Write_Data(Write_Data_15_0[5]), .Write_Select(Read_Select_1), .Clock(Clock),
    .Read_Data_1(Read_Data_1[5]), .Read_Data_2(Read_Data_2[5]), .Read_Select_1(Read_Select_2),
    .Read_Select_2(Write_Select));
  _1x1_SRAM u_1x1_sram_7 (
    .Write_Data(Write_Data_15_0[9]), .Write_Select(Read_Select_1), .Clock(Clock),
    .Read_Data_1(Read_Data_1[9]), .Read_Data_2(Read_Data_2[9]), .Read_Select_1(Read_Select_2),
    .Read_Select_2(Write_Select));
  _1x1_SRAM u_1x1_sram_8 (
    .Write_Data(Write_Data_15_0[13]), .Write_Select(Read_Select_1), .Clock(Clock),
    .Read_Data_1(Read_Data_1[13]), .Read_Data_2(Read_Data_2[13]), .Read_Select_1(Read_Select_2),
    .Read_Select_2(Write_Select));
  _1x1_SRAM u_1x1_sram_9 (
    .Write_Data(Write_Data_15_0[2]), .Write_Select(Read_Select_1), .Clock(Clock),
    .Read_Data_1(Read_Data_1[2]), .Read_Data_2(Read_Data_2[2]), .Read_Select_1(Read_Select_2),
    .Read_Select_2(Write_Select));
  _1x1_SRAM u_1x1_sram_10 (
    .Write_Data(Write_Data_15_0[6]), .Write_Select(Read_Select_1), .Clock(Clock),
    .Read_Data_1(Read_Data_1[6]), .Read_Data_2(Read_Data_2[6]), .Read_Select_1(Read_Select_2),
    .Read_Select_2(Write_Select));
  _1x1_SRAM u_1x1_sram_11 (
    .Write_Data(Write_Data_15_0[10]), .Write_Select(Read_Select_1), .Clock(Clock),
    .Read_Data_1(Read_Data_1[10]), .Read_Data_2(Read_Data_2[10]), .Read_Select_1(Read_Select_2),
    .Read_Select_2(Write_Select));
  _1x1_SRAM u_1x1_sram_12 (
    .Write_Data(Write_Data_15_0[14]), .Write_Select(Read_Select_1), .Clock(Clock),
    .Read_Data_1(Read_Data_1[14]), .Read_Data_2(Read_Data_2[14]), .Read_Select_1(Read_Select_2),
    .Read_Select_2(Write_Select));
  _1x1_SRAM u_1x1_sram_13 (
    .Write_Data(Write_Data_15_0[3]), .Write_Select(Read_Select_1), .Clock(Clock),
    .Read_Data_1(Read_Data_1[3]), .Read_Data_2(Read_Data_2[3]), .Read_Select_1(Read_Select_2),
    .Read_Select_2(Write_Select));
  _1x1_SRAM u_1x1_sram_14 (
    .Write_Data(Write_Data_15_0[7]), .Write_Select(Read_Select_1), .Clock(Clock),
    .Read_Data_1(Read_Data_1[7]), .Read_Data_2(Read_Data_2[7]), .Read_Select_1(Read_Select_2),
    .Read_Select_2(Write_Select));
  _1x1_SRAM u_1x1_sram_15 (
    .Write_Data(Write_Data_15_0[11]), .Write_Select(Read_Select_1), .Clock(Clock),
    .Read_Data_1(Read_Data_1[11]), .Read_Data_2(Read_Data_2[11]), .Read_Select_1(Read_Select_2),
    .Read_Select_2(Write_Select));
  _1x1_SRAM u_1x1_sram_16 (
    .Write_Data(Write_Data_15_0[15]), .Write_Select(Read_Select_1), .Clock(Clock),
    .Read_Data_1(Read_Data_1[15]), .Read_Data_2(Read_Data_2[15]), .Read_Select_1(Read_Select_2),
    .Read_Select_2(Write_Select));

  // Other names for the same wires on the sheet: CLK = Clock; RD1_0 = Read_Data_1[0]; RD1_1 = Read_Data_1[1];
  //   RD1_2 = Read_Data_1[2]; RD1_3 = Read_Data_1[3]; RD1_4 = Read_Data_1[4]; RD1_5 = Read_Data_1[5];
  //   RD1_6 = Read_Data_1[6]; RD1_7 = Read_Data_1[7]; RD1_8 = Read_Data_1[8]; RD1_9 = Read_Data_1[9];
  //   RD1_10 = Read_Data_1[10]; RD1_11 = Read_Data_1[11]; RD1_12 = Read_Data_1[12]; RD1_13 = Read_Data_1[13];
  //   RD1_14 = Read_Data_1[14]; RD1_15 = Read_Data_1[15]; RD2_0 = Read_Data_2[0]; RD2_1 = Read_Data_2[1];
  //   RD2_2 = Read_Data_2[2]; RD2_3 = Read_Data_2[3]; RD2_4 = Read_Data_2[4]; RD2_5 = Read_Data_2[5];
  //   RD2_6 = Read_Data_2[6]; RD2_7 = Read_Data_2[7]; RD2_8 = Read_Data_2[8]; RD2_9 = Read_Data_2[9];
  //   RD2_10 = Read_Data_2[10]; RD2_11 = Read_Data_2[11]; RD2_12 = Read_Data_2[12]; RD2_13 = Read_Data_2[13];
  //   RD2_14 = Read_Data_2[14]; RD2_15 = Read_Data_2[15]; RS1 = Read_Select_2; RS2 = Write_Select;
  //   D0 = Write_Data_15_0[0]; D1 = Write_Data_15_0[1]; D2 = Write_Data_15_0[2]; D3 = Write_Data_15_0[3];
  //   D4 = Write_Data_15_0[4]; D5 = Write_Data_15_0[5]; D6 = Write_Data_15_0[6]; D7 = Write_Data_15_0[7];
  //   D8 = Write_Data_15_0[8]; D9 = Write_Data_15_0[9]; D10 = Write_Data_15_0[10]; D11 = Write_Data_15_0[11];
  //   D12 = Write_Data_15_0[12]; D13 = Write_Data_15_0[13]; D14 = Write_Data_15_0[14]; D15 = Write_Data_15_0[15];
  //   WS = Read_Select_1
endmodule

module _1x16_SRAM_Testing (
  input  [15:0] Write_Data_15_0,
  input  in_2,
  input  in_3,
  input  in_4,
  input  in_5,
  output [15:0] Read_Data_1,
  output [15:0] Read_Data_2
);

  _1x16_SRAM u_1x16_sram_1 (
    .Write_Data_15_0(Write_Data_15_0), .Read_Select_1(in_2), .Read_Select_2(in_3), .Write_Select(in_4),
    .Clock(in_5), .Read_Data_1(Read_Data_1), .Read_Data_2(Read_Data_2));
endmodule

module _8x16_SRAM (
  input  [15:0] Write_Data_15_0,
  input  [2:0] Read_Address_1_2_0,
  input  [2:0] Read_Address_2_2_0,
  input  Write_Enable,
  input  [2:0] Write_Address_2_0,
  input  Clock,
  output [15:0] Read_Data_1_15_0,
  output [15:0] Read_Data_2_15_0
);

  wire R1_0, R1_1, R1_2, R1_3, R1_4, R1_5, R1_6, R1_7, R2_0, R2_1, R2_2, R2_3, R2_4, R2_5, R2_6, R2_7, W0,
       W1, W2, W3, W4, W5, W6, W7;
  wire [15:0] RD1_0, RD1_1, RD1_2, RD1_3, RD1_4, RD1_5, RD1_6, RD1_7, RD2_0, RD2_1, RD2_2, RD2_3, RD2_4,
       RD2_5, RD2_6, RD2_7;

  Decoder #(.select(3), .enable("false")) decoder_1 (
    .out0(R1_0), .out1(R1_1), .out2(R1_2), .out3(R1_3), .out4(R1_4), .out5(R1_5), .out6(R1_6), .out7(R1_7),
    .sel(Read_Address_1_2_0));
  Decoder #(.select(3), .enable("false")) decoder_2 (
    .out0(R2_0), .out1(R2_1), .out2(R2_2), .out3(R2_3), .out4(R2_4), .out5(R2_5), .out6(R2_6), .out7(R2_7),
    .sel(Read_Address_2_2_0));
  Decoder #(.select(3)) decoder_3 (
    .out0(W0), .out1(W1), .out2(W2), .out3(W3), .out4(W4), .out5(W5), .out6(W6), .out7(W7),
    .sel(Write_Address_2_0), .en(Write_Enable));
  _1x16_SRAM u_1x16_sram_1 (
    .Write_Data_15_0(Write_Data_15_0), .Read_Select_1(W0), .Read_Select_2(R1_0), .Write_Select(R2_0),
    .Clock(Clock), .Read_Data_1(RD1_0), .Read_Data_2(RD2_0));
  _1x16_SRAM u_1x16_sram_2 (
    .Write_Data_15_0(Write_Data_15_0), .Read_Select_1(W1), .Read_Select_2(R1_1), .Write_Select(R2_1),
    .Clock(Clock), .Read_Data_1(RD1_1), .Read_Data_2(RD2_1));
  _1x16_SRAM u_1x16_sram_3 (
    .Write_Data_15_0(Write_Data_15_0), .Read_Select_1(W2), .Read_Select_2(R1_2), .Write_Select(R2_2),
    .Clock(Clock), .Read_Data_1(RD1_2), .Read_Data_2(RD2_2));
  _1x16_SRAM u_1x16_sram_4 (
    .Write_Data_15_0(Write_Data_15_0), .Read_Select_1(W3), .Read_Select_2(R1_3), .Write_Select(R2_3),
    .Clock(Clock), .Read_Data_1(RD1_3), .Read_Data_2(RD2_3));
  _1x16_SRAM u_1x16_sram_5 (
    .Write_Data_15_0(Write_Data_15_0), .Read_Select_1(W4), .Read_Select_2(R1_4), .Write_Select(R2_4),
    .Clock(Clock), .Read_Data_1(RD1_4), .Read_Data_2(RD2_4));
  _1x16_SRAM u_1x16_sram_6 (
    .Write_Data_15_0(Write_Data_15_0), .Read_Select_1(W5), .Read_Select_2(R1_5), .Write_Select(R2_5),
    .Clock(Clock), .Read_Data_1(RD1_5), .Read_Data_2(RD2_5));
  _1x16_SRAM u_1x16_sram_7 (
    .Write_Data_15_0(Write_Data_15_0), .Read_Select_1(W6), .Read_Select_2(R1_6), .Write_Select(R2_6),
    .Clock(Clock), .Read_Data_1(RD1_6), .Read_Data_2(RD2_6));
  _1x16_SRAM u_1x16_sram_8 (
    .Write_Data_15_0(Write_Data_15_0), .Read_Select_1(W7), .Read_Select_2(R1_7), .Write_Select(R2_7),
    .Clock(Clock), .Read_Data_1(RD1_7), .Read_Data_2(RD2_7));
  assign Read_Data_1_15_0 = RD1_0 | RD1_1 | RD1_2 | RD1_3 | RD1_4 | RD1_5 | RD1_6 | RD1_7;  // OR_Gate or_1, 16 bits wide
  assign Read_Data_2_15_0 = RD2_0 | RD2_1 | RD2_2 | RD2_3 | RD2_4 | RD2_5 | RD2_6 | RD2_7;  // OR_Gate or_2, 16 bits wide

  // Other names for the same wires on the sheet: CLK = Clock
endmodule

module _8x16_SRAM_Testing (
  input  [2:0] Read_Address_1_2_0,
  input  [2:0] Read_Address_2_2_0,
  input  [2:0] Write_Address_2_0,
  input  [15:0] Write_Data_15_0,
  input  Write_Enable,
  input  Clock,
  output [15:0] Read_Data_1_15_0,
  output [15:0] Read_Data2_15_0
);

  _8x16_SRAM u_8x16_sram_1 (
    .Write_Data_15_0(Write_Data_15_0), .Read_Address_1_2_0(Read_Address_1_2_0),
    .Read_Address_2_2_0(Read_Address_2_2_0), .Write_Enable(Write_Enable),
    .Write_Address_2_0(Write_Address_2_0), .Clock(Clock), .Read_Data_1_15_0(Read_Data_1_15_0),
    .Read_Data_2_15_0(Read_Data2_15_0));
endmodule

module _3_bit_Counter (
  input  [2:0] Din_2_0,
  input  Clock,
  output [2:0] Dout_2_0
);

  _1_bit_Register u_1_bit_register_1 (.Din(Din_2_0[0]), .Sel(1'b1), .Clock(Clock), .Dout(Dout_2_0[0]));
  _1_bit_Register u_1_bit_register_2 (.Din(Din_2_0[1]), .Sel(1'b1), .Clock(Clock), .Dout(Dout_2_0[1]));
  _1_bit_Register u_1_bit_register_3 (.Din(Din_2_0[2]), .Sel(1'b1), .Clock(Clock), .Dout(Dout_2_0[2]));
endmodule

module _3_bit_PC_Adder (
  input  [2:0] Input_Address__2_0,
  output [2:0] Output_Address__2_0
);

  wire [2:0] bit_extender_1_out;

  assign bit_extender_1_out = {{2{1'b0}}, 1'b1};  // Bit_Extender bit_extender_1
  Adder #(.width(3)) adder_1 (
    .a(Input_Address__2_0), .b(bit_extender_1_out), .out(Output_Address__2_0), .cin(1'b0));  // open: cout
endmodule

module ROM (
  input  Clock,
  input  PC_Enable,
  output [2:0] Physical_Address,
  output [15:0] Data,
  output Write_Enable,
  output PC_Clock
);

  Counter #(.width(3), .max('h7), .ongoal("stay")) counter_1 (
    .Q(Physical_Address), .clk(Clock));  // open: load, D, count, carry, clr
  not not_1 (Write_Enable, PC_Enable);
  and and_1 (PC_Clock, Clock, PC_Enable);
  ROM_part #(.addrWidth(3), .dataWidth(16)) rom_1 (.addr(Physical_Address), .data(Data));  // open: sel

  // Notes on the sheet:
  //   contents of rom_1 (hex, n*v repeats v):
  //   40 ffb0 21 ffb0 30 40 ff81 41
endmodule

module Control_Unit (
  input  [2:0] Opcode_2_0,
  input  ZF,
  output Op,
  output Imm_Sel,
  output WE,
  output Jmp_Sel
);

  wire and_2_out, and_3_out, not_1_out, not_2_out, not_3_out, not_4_out, not_5_out;

  not not_1 (not_1_out, Opcode_2_0[2]);
  not not_2 (not_2_out, Opcode_2_0[2]);
  not not_3 (not_3_out, Opcode_2_0[1]);
  not not_4 (not_4_out, Opcode_2_0[1]);
  and and_1 (Imm_Sel, not_1_out, Opcode_2_0[1]);
  and and_2 (and_2_out, not_2_out, not_3_out);
  and and_3 (and_3_out, Opcode_2_0[2], not_4_out);
  not not_5 (not_5_out, Opcode_2_0[0]);
  or or_1 (WE, Imm_Sel, and_2_out);
  and and_4 (Jmp_Sel, and_3_out, not_5_out, ZF);

  assign Op = Opcode_2_0[0];
endmodule

module CPU (
  input  [2:0] Write_Address_2_0,
  input  [15:0] Write_Data_15_0,
  input  Write_Enable,
  input  Clock,
  input  CPU_Enable
);

  wire alu_1_carry_flag, alu_1_sign_flag, alu_1_zero_flag, CF, CPU_CLK, Imm_Sel, JMP_Adder, Jmp_Sel, OP, SF,
       WE, ZF;
  wire [2:0] bit_extender_1_out, multiplexer_1_out, n3_bit_counter_1_dout_2_0,
       n3_bit_pc_adder_1_output_address__2_0;
  wire [4:0] alu_1_r__4_0, multiplexer_2_out, register_set_with_3_5_bit_registers_1_a,
       register_set_with_3_5_bit_registers_1_b;
  wire [15:0] n8x16_sram_1_read_data_1_15_0;

  Multiplexer #(.width(3), .enable("false")) multiplexer_1 (
    .in0(n3_bit_pc_adder_1_output_address__2_0), .in1(bit_extender_1_out), .out(multiplexer_1_out),
    .sel(Jmp_Sel));
  assign bit_extender_1_out = {{2{1'b0}}, JMP_Adder};  // Bit_Extender bit_extender_1
  _3_bit_PC_Adder u_3_bit_pc_adder_1 (
    .Input_Address__2_0(n3_bit_counter_1_dout_2_0),
    .Output_Address__2_0(n3_bit_pc_adder_1_output_address__2_0));
  _3_bit_Counter u_3_bit_counter_1 (.Din_2_0(multiplexer_1_out), .Clock(CPU_CLK), .Dout_2_0(n3_bit_counter_1_dout_2_0));
  and and_1 (CPU_CLK, Clock, CPU_Enable);
  _8x16_SRAM u_8x16_sram_1 (
    .Write_Data_15_0(Write_Data_15_0), .Read_Address_1_2_0(n3_bit_counter_1_dout_2_0),
    .Write_Enable(Write_Enable), .Write_Address_2_0(Write_Address_2_0), .Clock(Clock),
    .Read_Data_1_15_0({n8x16_sram_1_read_data_1_15_0[15:14], JMP_Adder, n8x16_sram_1_read_data_1_15_0[12:0]}));  // open: Read_Address_2_2_0, Read_Data_2_15_0
  Register_Set_with_3__5_bit_Registers register_set_with_3_5_bit_registers_1 (
    .WRD(alu_1_r__4_0), .WE(WE), .WR(n8x16_sram_1_read_data_1_15_0[12:11]), .Clock(CPU_CLK),
    .RA(n8x16_sram_1_read_data_1_15_0[12:11]), .RB(n8x16_sram_1_read_data_1_15_0[10:9]),
    .A(register_set_with_3_5_bit_registers_1_a), .B(register_set_with_3_5_bit_registers_1_b));
  ALU alu_1 (
    .A__4_0(register_set_with_3_5_bit_registers_1_a), .OP_1_0(OP), .R__4_0(alu_1_r__4_0),
    .Sign_Flag(alu_1_sign_flag), .Zero_Flag(alu_1_zero_flag), .B_4_0(multiplexer_2_out),
    .Carry_Flag(alu_1_carry_flag));
  Flag_Registor flag_registor_1 (
    .CFin(alu_1_carry_flag), .SFin(alu_1_sign_flag), .ZFin(alu_1_zero_flag), .Clock(CPU_CLK), .CFout(CF),
    .SFout(SF), .ZFout(ZF));
  Multiplexer #(.width(5), .disabled(0), .enable("false")) multiplexer_2 (
    .in0(register_set_with_3_5_bit_registers_1_b), .in1(n8x16_sram_1_read_data_1_15_0[10:6]),
    .out(multiplexer_2_out), .sel(Imm_Sel));
  Control_Unit control_unit_1 (
    .Opcode_2_0({n8x16_sram_1_read_data_1_15_0[15:14], JMP_Adder}), .Op(OP), .Imm_Sel(Imm_Sel), .WE(WE),
    .Jmp_Sel(Jmp_Sel), .ZF(ZF));

  // Other names for the same wires on the sheet: CLK = Clock

  // Notes on the sheet:
  //   Opcode 1st 2 bits=10 + Opcode last 1 bit= JZ(0)
  //   Branching Mode JZ= 10 0 000 0000000000
  //   Opcode 1st 2 bits=00 + Opcode last 1 bit= NOT(0), ROR(1)
  //   Opcode 1st 2 bits=01 + Opcode last 1 bit= NOT(0), ROR(1)
  //   Branching Mode: Opcode (2 bits + 1 bit) + Address (3 bits) + Unused (10 bits)
  //   Register Mode: Opcode (2 bits + 1 bit) + Register RA (2 bits) + Register RB (2 bits) + Unused (9 bits)
  //   Register Mode NOT= 00 0 00 00 000000000      Register Mode ROR= 00 1 00 01 000000000
  //   Immediate Mode: Opcode (2 bits + 1 bit) + Register RA (2 bits) + Constant (5 bits) + Unused (6 bits)
  //   Immediate Mode NOT= 01 0 00 00000 000000      Immedite Mode ROR= 01 1 00 00001 000000
endmodule

module Flag_Registor (
  input  CFin,
  input  SFin,
  input  ZFin,
  input  Clock,
  output CFout,
  output SFout,
  output ZFout
);

  _1_bit_Register u_1_bit_register_1 (.Din(CFin), .Sel(1'b1), .Clock(Clock), .Dout(CFout));
  _1_bit_Register u_1_bit_register_2 (.Din(SFin), .Sel(1'b1), .Clock(Clock), .Dout(SFout));
  _1_bit_Register u_1_bit_register_3 (.Din(ZFin), .Sel(1'b1), .Clock(Clock), .Dout(ZFout));
endmodule
